# Fritzing sketch Schematic (saved by Fritzing 0.9.4)
breadboards: 1

parts:
  Main_Board = Arduino Uno (Rev3)
  PWM_Output = Camdenboss CTB0158-4 [part_number="PWM Header" package=THT]
  Main_Display = LCD screen
  Main_Thermistor = Temperature Sensor (Thermistor) [thermistor_type=NTC package=THT]
  10K = Resistor [tolerance=±5% resistance=10k package="2010 [SMD]"]
  1K = Resistor [tolerance=±5% resistance=1k package="2010 [SMD]"]

nets:
  N1: Main_Board.A0, Main_Thermistor.pin_1, 10K.Pin_0
  N2: Main_Board.D9_PWM, PWM_Output.pin4
  N3: Main_Board.D11_PWM/MOSI, Main_Display.E
  N4: Main_Board.D12/MISO, Main_Display.RS
  GND: Main_Board.GND, Main_Display.VSS, Main_Thermistor.pin_0, 1K.Pin_0
  N5: Main_Board.AREF, Main_Board.3V3, Main_Display.LED+, 10K.Pin_1
  N6: Main_Board.D2, PWM_Output.pin3
  N7: Main_Board.D3_PWM, Main_Display.DB7
  N8: Main_Board.D4, Main_Display.DB6
  N9: Main_Board.D5_PWM, Main_Display.DB5
  N10: Main_Board.D6_PWM, Main_Display.DB4
  5V: Main_Board.5V, Main_Display.VDD
  N11: Main_Display.V0, Main_Display.R/W, Main_Display.LED-, 1K.Pin_1
